# Fritzing sketch wiring (saved by Fritzing 0.9.3b)
breadboards: 1

parts:
  Part1 = SRF05 Ultrasonic Rangefinder
  R1 = Resistor [tolerance=±5% resistance=1k package=THT]
  R2 = Resistor [tolerance=±5% resistance=2.2k package=THT]
  M2 = DC Motor
  U1 = DC-DC_CONVERTER [package=dc-dc_converter]
  VCC1 = 4 x AAA Battery Mount
  M3 = DC Motor
  VCC2 = Battery
  BAT1 = Battery Holders [package=battery-aa]  # not connected
  Raspberry_Pi_1 = Raspberry Pi 2
  S1 = H-Bridge with L298N

nets:
  5V: Part1.VCC, U1.ON_OFF, Raspberry_Pi_1.5V, S1.5V
  N1: Part1.Trig, Raspberry_Pi_1.GPIO27
  N2: Part1.Echo, R1.Pin_0
  GND: Part1.GND, R2.Pin_0, U1.PGOOD, VCC1.-, Raspberry_Pi_1.GND, S1.GND
  N3: R1.Pin_1, R2.Pin_1, Raspberry_Pi_1.GPIO22
  N4: M2.pin_1, S1.M1-02
  N5: M2.pin_2, S1.M1-01
  N6: U1.SENSE, VCC2.+
  N7: U1.TRIM, VCC2.-
  N8: VCC1.+, S1.12V
  N9: M3.pin_1, S1.M2-02
  N10: M3.pin_2, S1.M2-01
  N11: Raspberry_Pi_1.GPIO5, S1.IN1
  N12: Raspberry_Pi_1.GPIO6, S1.IN2
  N13: Raspberry_Pi_1.GPIO13, S1.IN3
  N14: Raspberry_Pi_1.GPIO26, S1.IN4
  N15: Raspberry_Pi_1.GPIO16, S1.ENB
  N16: Raspberry_Pi_1.GPIO12, S1.ENA

notes:
  Wheel Encoder 1
  Wheel Encoder 2

custom parts:
  H-Bridge with L298N: h-bridge
